# Fritzing sketch transmitter (saved by Fritzing 0.9.3b)

parts:
  Componente2 = Arduino Nano (Rev3.0)
  Componente3 = Thumb Joystick
  Componente4 = Thumb Joystick
  Componente5 = NRF24L01+ Breakout Board
  LED1 = LED - 3mm [color="Red (633nm)" package="3 mm [THT]"]
  LED2 = LED - 3mm [color="Red (633nm)" package="3 mm [THT]"]
  LED3 = LED - 3mm [color="Red (633nm)" package="3 mm [THT]"]

nets:
  GND: Componente2.GND, Componente3.GND, Componente4.GND, Componente5.GND, LED1.anode, LED2.anode, LED3.anode
  N1: Componente2.D2, Componente4.SEL
  N2: Componente2.D4, Componente3.SEL
  N3: Componente2.D6, LED3.cathode
  N4: Componente2.D7, LED2.cathode
  N5: Componente2.D8, LED1.cathode
  N6: Componente2.D9, Componente5.CE
  N7: Componente2.D10, Componente5.CS
  N8: Componente2.D11/MOSI, Componente5.MOSI
  N9: Componente2.D12/MISO, Componente5.MISO
  VCC: Componente2.5V, Componente3.VCC, Componente4.VCC
  N10: Componente2.A3, Componente3.HORZ
  N11: Componente2.A2, Componente3.VERT
  N12: Componente2.A1, Componente4.HORZ
  N13: Componente2.A0, Componente4.VERT
  3V3: Componente2.3V3, Componente5.VCC
  N14: Componente2.D13/SCK, Componente5.SCK
